# Fritzing sketch schematic2 (saved by Fritzing 1.0.0rc)
breadboards: 1

parts:
  J1 = Basic Servo
  J2 = Basic Servo
  LED1 = smd LED [color="Red (633nm)" package="1206 [SMD]"]
  LED2 = smd LED [color="Red (633nm)" package="1206 [SMD]"]
  IC1 = ULN2003A [package="DIP16 [THT]"]
  J3 = Basic Servo
  LED3 = smd LED [color="Red (633nm)" package="1206 [SMD]"]
  WeMos_D1_Mini1 = WeMos D1 Mini  # not connected

nets:
  GND: J1.gnd, J2.gnd, J3.gnd
  VCC: J1.vcc, J2.vcc, IC1.0V, J3.vcc
  N1: LED1.cathode, IC1.Out_7
  N2: LED1.anode, LED2.anode, LED3.anode
  N3: LED2.cathode, IC1.Out_4
  N4: IC1.Out_1, LED3.cathode
